# Fritzing sketch Joystick RGB (saved by Fritzing 0.9.3b)
breadboards: 1

parts:
  Part1 = Arduino Uno (Rev3)
  LED1 = RGB LED - (4 legs) [package="5 mm [THT]"]  # not connected
  R1 = Trimmer Potentiometer [maximum_resistance=10kΩ package=THT]
  Part2 = Thumb Joystick

nets:
  N1: Part1.A0, R1.wiper
  N2: Part1.A1, Part2.HORZ
  N3: Part1.A2, Part2.VERT
  5V: Part1.5V, R1.leg1, Part2.VCC
  GND: Part1.GND, R1.leg2, Part2.GND
